# Fritzing sketch TimerCircuit (saved by Fritzing 0.9.3b)
breadboards: 1

parts:
  Arduino_UNO = Arduino Uno (Rev3)
  LCD1 = LCD screen
  R1 = Trimmer Potentiometer [maximum_resistance=10kΩ package=THT]
  R2 = Resistor [tolerance=±5% resistance=220 package=THT]
  R4 = Trimmer Potentiometer [maximum_resistance=10kΩ package=THT]
  S1 = Pushbutton [package="[THT]"]
  S2 = Pushbutton [package="[THT]"]
  R3 = Resistor [tolerance=±5% resistance=220 package=THT]
  R5 = Resistor [tolerance=±5% resistance=220 package=THT]
  J1 = Piezo Speaker
  R6 = Resistor [tolerance=±5% resistance=100 package=THT]

nets:
  N1: Arduino_UNO.D8, R4.wiper
  N2: Arduino_UNO.D9_PWM, LCD1.LED+, R2.Pin_0, R2.Pin_1
  N3: Arduino_UNO.D10_PWM/SS, S1.Pin_1, S1.Pin_2, R3.Pin_0
  N4: Arduino_UNO.D11_PWM/MOSI, S2.Pin_1, S2.Pin_2, R5.Pin_0
  N5: Arduino_UNO.D12/MISO, J1.pin2
  GND: Arduino_UNO.GND, LCD1.VSS, LCD1.R/W, LCD1.LED-, R1.leg1, R4.leg1, R3.Pin_1, R5.Pin_1, R6.Pin_0
  N6: Arduino_UNO.D2, LCD1.RS
  N7: Arduino_UNO.D3_PWM, LCD1.E
  N8: Arduino_UNO.D4, LCD1.DB4
  N9: Arduino_UNO.D5_PWM, LCD1.DB5
  N10: Arduino_UNO.D6_PWM, LCD1.DB6
  N11: Arduino_UNO.D7, LCD1.DB7
  5V: Arduino_UNO.5V, LCD1.VDD, R1.leg2, R4.leg2, S1.Pin_3, S1.Pin_4, S2.Pin_3, S2.Pin_4
  N12: LCD1.V0, R1.wiper
